# Fritzing sketch SingleDigitClock (saved by Fritzing 0.9.4)
circuit board: 8cm x 8cm
breadboards: 1

parts:
  JP3 = Header 2 [part_number="12V POWER" package=jst-2-pth-kit]
  Q0 = NPN-Transistor [package="TO92 [THT]"]
  Q2 = NPN-Transistor [package="TO92 [THT]"]
  Q3 = NPN-Transistor [package="TO92 [THT]"]
  Q4 = NPN-Transistor [package="TO92 [THT]"]
  Q5 = NPN-Transistor [package="TO92 [THT]"]
  Q6 = NPN-Transistor [package="TO92 [THT]"]
  J1 = female pin header, 9 pins [form="♀ (female)" part_number=7-SEGMENT]
  J2 = female pin header, 6 pins [form="♀ (female)" part_number="FRONT PANEL"]
  Q7 = NPN-Transistor [package="TO92 [THT]"]
  LED = LED - 5mm [color="Red (633nm)" part_number=SECONDS package="5 mm [THT]"]
  R10 = Resistor [tolerance=±1% resistance=10k package="1206 [SMD]"]
  R9 = Resistor [tolerance=±1% resistance=10k package="1206 [SMD]"]
  R0 = Resistor [tolerance=±1% resistance=5.6k package="1206 [SMD]"]
  R1 = Resistor [tolerance=±1% resistance=5.6k package="1206 [SMD]"]
  R2 = Resistor [tolerance=±1% resistance=5.6k package="1206 [SMD]"]
  R4 = Resistor [tolerance=±1% resistance=5.6k package="1206 [SMD]"]
  R3 = Resistor [tolerance=±1% resistance=5.6k package="1206 [SMD]"]
  R5 = Resistor [tolerance=±1% resistance=5.6k package="1206 [SMD]"]
  R6 = Resistor [tolerance=±1% resistance=5.6k package="1206 [SMD]"]
  R7 = Resistor [tolerance=±1% resistance=5.6k package="1206 [SMD]"]
  R8 = Resistor [tolerance=±1% resistance=220 package="1206 [SMD]"]
  Arduino_Nano = Arduino Nano (Rev3.0)
  Q1 = NPN-Transistor [package="TO92 [THT]"]
  VALUE = Pushbutton [package="[THT]"]
  SET = Pushbutton [package="[THT]"]
  C2 = Ceramic Capacitor [capacitance=100nF package="1206 [SMD, multilayer]"]
  C1 = Ceramic Capacitor [capacitance=3.3µF package="1206 [SMD, multilayer]"]
  U1 = Voltage Regulator - 5V [part_number=L7808 package="TO220 [THT]"]
  ZS-042_RTC = ZS-042 RTC Module

nets:
  GND: JP3.1, Q0.E, Q2.E, Q3.E, Q4.E, Q5.E, Q6.E, J1.pin9, Q7.E, R10.Pin_0, R9.Pin_0, Arduino_Nano.GND, Q1.E, C2.0, C1.0, U1.GND, ZS-042_RTC.GND
  12V: JP3.2, J1.pin1, C1.1, U1.input_voltage
  N1: Q0.B, R0.Pin_0
  SegA: Q0.C, J1.pin2
  N2: Q2.B, R2.Pin_0
  SegC: Q2.C, J1.pin4
  N3: Q3.B, R3.Pin_0
  SegD: Q3.C, J1.pin5
  N4: Q4.B, R4.Pin_0
  SegE: Q4.C, J1.pin6
  N5: Q5.B, R5.Pin_0
  SegF: Q5.C, J1.pin7
  N6: Q6.B, R6.Pin_0
  SegG: Q6.C, J1.pin8
  SegB: J1.pin3, Q1.C
  5V: J2.pin1, J2.pin3, R8.Pin_0, Arduino_Nano.5V, VALUE.Pin_1, VALUE.Pin_2, SET.Pin_1, SET.Pin_2, ZS-042_RTC.VCC
  SET BUTTON: J2.pin2, R10.Pin_1, Arduino_Nano.D9, SET.Pin_3
  VALUE BUTTON: J2.pin4, R9.Pin_1, Arduino_Nano.D8, VALUE.Pin_3
  N7: J2.pin5, LED.anode, R8.Pin_1
  N8: J2.pin6, Q7.C, LED.cathode
  N9: Q7.B, R7.Pin_1
  D0: R0.Pin_1, Arduino_Nano.D0/RX
  N10: R1.Pin_0, Q1.B
  D1: R1.Pin_1, Arduino_Nano.D1/TX
  D2: R2.Pin_1, Arduino_Nano.D2
  D4: R4.Pin_1, Arduino_Nano.D4
  D3: R3.Pin_1, Arduino_Nano.D3
  D5: R5.Pin_1, Arduino_Nano.D5
  D6: R6.Pin_1, Arduino_Nano.D6
  SQW: R7.Pin_0, ZS-042_RTC.SQW
  8V: Arduino_Nano.VIN, C2.1, U1.output_voltage
  N11: Arduino_Nano.A5, ZS-042_RTC.SCL
  N12: Arduino_Nano.A4, ZS-042_RTC.SDA

notes:
  Single Digit Clock, What I Made Today: single digit clock
  S+ S- V+ V- L+ L-
  Front Panel
  12V IN
  12v A  B  C  D  E  F  G  0v
  Single Digit Clock  v1.0
  WhatIMade.Today, Mar 2020
  D0 D1
  Gnd Vin
  A4 A5
  D9 D8
  5v
  8v
  12v
  GND
  L7808CV
  RTC MODULE
