# Fritzing sketch ArduinoConnectingBoardRtc_v3.0 (saved by Fritzing 0.9.4)
circuit board: 7.98286cm x 4.41476cm
breadboards: 1

parts:
  JP1 = Header 2 [part_number=POWER package=jst-2-pth-kit]
  U1 = Arduino Nano (Rev3.0) [part_number="Arduino Nano"]
  JP3 = Header 12 [package=1x12_machine-pin-header_lock.004]
  JP2 = Header 12 [package=1x12_machine-pin-header_lock.004]
  MODE = Pushbutton [package="[THT]"]
  NEXT = Pushbutton [package="[THT]"]
  R1 = Resistor [tolerance=±5% resistance=10k package="1206 [SMD]"]
  R2 = Resistor [tolerance=±5% resistance=10k package="1206 [SMD]"]
  ZS-042_RTC1 = ZS-042 RTC Module

nets:
  GND: JP1.1, U1.GND, JP3.11, JP2.11, MODE.Pin_1, MODE.Pin_2, NEXT.Pin_1, NEXT.Pin_2, ZS-042_RTC1.GND
  VIN: JP1.2, U1.VIN
  D2: U1.D2, JP3.6
  D3: U1.D3, JP3.5
  D4: U1.D4, JP2.1
  D5: U1.D5, JP2.2
  D6: U1.D6, JP2.3
  D7: U1.D7, JP2.4
  D8: U1.D8, JP2.5
  D9: U1.D9, JP2.6
  D10: U1.D10, JP2.7
  D11: U1.D11/MOSI, JP2.8
  D12: U1.D12/MISO, JP3.8
  5V: U1.5V, JP3.12, JP2.12, R1.Pin_0, R2.Pin_0, ZS-042_RTC1.VCC
  A7: U1.A7, NEXT.Pin_3, NEXT.Pin_4, R2.Pin_1
  A6: U1.A6, MODE.Pin_3, MODE.Pin_4, R1.Pin_1
  SCL: U1.A5, ZS-042_RTC1.SCL
  SDA: U1.A4, ZS-042_RTC1.SDA
  N1: U1.A3, JP3.4
  N2: U1.A2, JP3.3
  N3: U1.A1, JP3.2
  N4: U1.A0, JP3.1
  D13: U1.D13/SCK, JP3.7

notes:
  V3, Dec 2019
  A0
  A1
  A2
  A3
  5v
  Gnd
  D10
  D11
  D12
  D13
  D4
  D5
  D6
  D7
  D8
  D9
  D2
  D3
  Vin
  Mike & Allan's
  D1
  VIN
  Arduino & RTC Board
  www.WhatIMade.today
