# Fritzing sketch BigLedFromChip (saved by Fritzing 0.9.3b)
circuit board: 6.90496cm x 5.06866cm
breadboards: 1

parts:
  JP6 = Header 12 [package=1x12_machine-pin-header_lock.004]
  JP7 = Header 12 [package=1x12_machine-pin-header_lock.004]
  JP8 = Header 12 [package=1x12_machine-pin-header_lock.004]
  JP9 = Header 12 [package=1x12_machine-pin-header_lock.004]
  IC4 = SHIFT REGISTER [package=dil16]
  IC3 = SHIFT REGISTER [package=dil16]
  R12 = Resistor [tolerance=±5% resistance=220 package="1206 [SMD]"]
  R19 = Resistor [tolerance=±5% resistance=220 package="1206 [SMD]"]
  R27 = Resistor [tolerance=±5% resistance=220 package="1206 [SMD]"]
  R18 = Resistor [tolerance=±5% resistance=220 package="1206 [SMD]"]
  R26 = Resistor [tolerance=±5% resistance=220 package="1206 [SMD]"]
  R25 = Resistor [tolerance=±5% resistance=220 package="1206 [SMD]"]
  R16 = Resistor [tolerance=±5% resistance=220 package="1206 [SMD]"]
  R17 = Resistor [tolerance=±5% resistance=220 package="1206 [SMD]"]
  R20 = Resistor [tolerance=±5% resistance=220 package="1206 [SMD]"]
  R21 = Resistor [tolerance=±5% resistance=220 package="1206 [SMD]"]
  R22 = Resistor [tolerance=±5% resistance=220 package="1206 [SMD]"]  # not connected
  R23 = Resistor [tolerance=±5% resistance=220 package="1206 [SMD]"]
  R24 = Resistor [tolerance=±5% resistance=220 package="1206 [SMD]"]
  R14 = Resistor [tolerance=±5% resistance=220 package="1206 [SMD]"]  # not connected
  R13 = Resistor [tolerance=±5% resistance=220 package="1206 [SMD]"]
  R15 = Resistor [tolerance=±5% resistance=220 package="1206 [SMD]"]
  JP10 = Header 12 [package=1x12_machine-pin-header_lock.004]

nets:
  N1: JP6.6, R20.Pin_1
  N2: JP6.7, R21.Pin_1
  N3: JP6.8, R23.Pin_1
  VCC: JP6.9, JP7.6, IC4.VCC, IC3.VCC, JP10.12
  N4: JP7.7, R26.Pin_0
  N5: JP7.8, R15.Pin_0
  N6: JP7.9, R17.Pin_1
  N7: JP8.5, R16.Pin_0
  N8: JP8.6, R27.Pin_0
  N9: JP8.8, R25.Pin_1
  N10: JP8.9, R24.Pin_0
  N11: JP9.6, R18.Pin_0
  N12: JP9.7, R13.Pin_1
  N13: JP9.9, R19.Pin_0
  N14: JP9.10, R12.Pin_0
  N15: IC4.QB, JP10.6
  N16: IC4.QC, JP10.7
  N17: IC4.QG, JP10.8
  N18: IC4.QH, JP10.5
  GND: IC4.GND, IC3.GND, JP10.11
  N19: IC4.QH*, R20.Pin_0
  N20: IC4.SCL, R21.Pin_0
  N21: IC4.SCK, R23.Pin_0
  N22: IC4.RCK, R24.Pin_1
  N23: IC4.G, R25.Pin_0
  N24: IC4.SER, R16.Pin_1
  N25: IC4.QA, R27.Pin_1
  N26: IC3.QB, JP10.2
  N27: IC3.QC, JP10.3
  N28: IC3.QG, JP10.4
  N29: IC3.QH, JP10.1
  N30: IC3.QH*, R26.Pin_1
  N31: IC3.SCL, R15.Pin_1
  N32: IC3.SCK, R17.Pin_0
  N33: IC3.RCK, R12.Pin_1
  N34: IC3.G, R19.Pin_1
  N35: IC3.SER, R18.Pin_1
  N36: IC3.QA, R13.Pin_0

notes:
  b
  a
  f
  .
  g
  c
  d
  e
  +
  GND
  Mike's LED Board V 2.0
  Apr. 2019
  A0
  A1
  A2
  A3
