# Fritzing sketch 8 pushbuttons (saved by Fritzing 0.9.3b)
circuit board: 6.88566cm x 5.36311cm
breadboards: 2

parts:
  S7 = Pushbutton [package="[THT]"]
  S6 = Pushbutton [package="[THT]"]
  S5 = Pushbutton [package="[THT]"]
  S4 = Pushbutton [package="[THT]"]
  S3 = Pushbutton [package="[THT]"]
  S2 = Pushbutton [package="[THT]"]
  S1 = Pushbutton [package="[THT]"]
  S0 = Pushbutton [package="[THT]"]
  R2 = Resistor [tolerance=±5% resistance=10k package=THT]
  R4 = Resistor [tolerance=±5% resistance=10k package=THT]
  R0 = Resistor [tolerance=±5% resistance=10k package=THT]
  R6 = Resistor [tolerance=±5% resistance=10k package=THT]
  R1 = Resistor [tolerance=±5% resistance=10k package=THT]
  R3 = Resistor [tolerance=±5% resistance=10k package=THT]
  R5 = Resistor [tolerance=±5% resistance=10k package=THT]
  R7 = Resistor [tolerance=±5% resistance=10k package=THT]
  74HC165 = IC, DIP package, 16 pins [chip_label=74HC165]
  Part1 = Arduino Uno (Rev3)
  LED1 = LED - 5mm [color="Red (633nm)" package="5 mm [THT]"]  # not connected
  LED2 = LED - 5mm [color="Red (633nm)" package="5 mm [THT]"]  # not connected
  LED3 = LED - 5mm [color="Red (633nm)" package="5 mm [THT]"]  # not connected
  LED4 = LED - 5mm [color="Red (633nm)" package="5 mm [THT]"]  # not connected
  LED5 = LED - 5mm [color="Red (633nm)" package="5 mm [THT]"]  # not connected
  LED6 = LED - 5mm [color="Red (633nm)" package="5 mm [THT]"]  # not connected
  LED7 = LED - 5mm [color="Red (633nm)" package="5 mm [THT]"]  # not connected
  LED8 = LED - 5mm [color="Red (633nm)" package="5 mm [THT]"]  # not connected

nets:
  N1: S7.Pin_1, S7.Pin_2, R7.Pin_0, 74HC165.pin6
  GND: S7.Pin_3, S7.Pin_4, S6.Pin_3, S6.Pin_4, S5.Pin_3, S5.Pin_4, S4.Pin_3, S4.Pin_4, S3.Pin_3, S3.Pin_4, S2.Pin_3, S2.Pin_4, S1.Pin_3, S1.Pin_4, S0.Pin_3, S0.Pin_4, 74HC165.pin8, Part1.GND
  N2: S6.Pin_1, S6.Pin_2, R6.Pin_0, 74HC165.pin5
  N3: S5.Pin_1, S5.Pin_2, R5.Pin_0, 74HC165.pin4
  N4: S4.Pin_1, S4.Pin_2, R4.Pin_0, 74HC165.pin3
  N5: S3.Pin_1, S3.Pin_2, R3.Pin_0, 74HC165.pin14
  N6: S2.Pin_1, S2.Pin_2, R2.Pin_0, 74HC165.pin13
  N7: S1.Pin_1, S1.Pin_2, R1.Pin_0, 74HC165.pin12
  N8: S0.Pin_1, S0.Pin_2, R0.Pin_0, 74HC165.pin11
  5V: R2.Pin_1, R4.Pin_1, R0.Pin_1, R6.Pin_1, R1.Pin_1, R3.Pin_1, R5.Pin_1, R7.Pin_1, 74HC165.pin16, Part1.5V
  N9: 74HC165.pin1, Part1.D10_PWM/SS
  N10: 74HC165.pin2, Part1.D13/SCK
  N11: 74HC165.pin9, Part1.D12/MISO
  N12: 74HC165.pin15, Part1.D9_PWM

notes:
  pin1 Vcc
  pin2 GND
  pin3 D9 CS-165 -> 15 CE red
  pin4 D10 Latch -> 1 PL orange
  pin5 D12 MISO -> 9 Q7 green
  pin6 D13 SCLK -> 2 CP blue
