# Fritzing sketch 8_led_74595 (saved by Fritzing 0.9.3b)
circuit board: 7.925cm x 5.30269cm
breadboards: 2

parts:
  LED4 = LED - 3mm [color="Red (633nm)" package="3 mm [THT]"]
  LED5 = LED - 3mm [color="Red (633nm)" package="3 mm [THT]"]
  LED6 = LED - 3mm [color="Red (633nm)" package="3 mm [THT]"]
  R0 = Resistor [tolerance=±5% resistance=220 package=THT]
  R2 = Resistor [tolerance=±5% resistance=220 package=THT]
  R3 = Resistor [tolerance=±5% resistance=220 package=THT]
  R4 = Resistor [tolerance=±5% resistance=220 package=THT]
  R5 = Resistor [tolerance=±5% resistance=220 package=THT]
  R7 = Resistor [tolerance=±5% resistance=220 package=THT]
  CONN1 = Header 6 [package=molex-1x6_lock]
  74595 = 74HC595 [package="DIP16 [THT]"]
  LED1 = LED - 3mm [color="Red (633nm)" package="3 mm [THT]"]
  LED0 = LED - 3mm [color="Red (633nm)" package="3 mm [THT]"]
  LED7 = LED - 3mm [color="Red (633nm)" package="3 mm [THT]"]
  LED3 = LED - 3mm [color="Red (633nm)" package="3 mm [THT]"]
  R1 = Resistor [tolerance=±5% resistance=220 package=THT]
  LED2 = LED - 3mm [color="Red (633nm)" package="3 mm [THT]"]
  R6 = Resistor [tolerance=±5% resistance=220 package=THT]
  Part1 = Arduino Uno (Rev3)

nets:
  GND: LED4.cathode, LED5.cathode, LED6.cathode, CONN1.2, 74595.GND, LED1.cathode, LED0.cathode, LED7.cathode, LED3.cathode, LED2.cathode, Part1.GND
  N1: LED4.anode, R4.Pin_1
  N2: LED5.anode, R5.Pin_1
  N3: LED6.anode, R6.Pin_1
  N4: R0.Pin_0, 74595.Q0
  N5: R0.Pin_1, LED0.anode
  N6: R2.Pin_0, 74595.Q2
  N7: R2.Pin_1, LED2.anode
  N8: R3.Pin_0, 74595.Q3
  N9: R3.Pin_1, LED3.anode
  N10: R4.Pin_0, 74595.Q4
  N11: R5.Pin_0, 74595.Q5
  N12: R7.Pin_0, 74595.Q7
  N13: R7.Pin_1, LED7.anode
  5V: CONN1.1, 74595.MR, 74595.VCC, Part1.5V, Part1.VIN
  N14: CONN1.3, 74595.OE, Part1.D8
  N15: CONN1.4, 74595.ST_CP, Part1.D10_PWM/SS
  N16: CONN1.5, 74595.DS, Part1.D11_PWM/MOSI
  N17: CONN1.6, 74595.SH_CP, Part1.D13/SCK
  N18: 74595.Q1, R1.Pin_0
  N19: 74595.Q6, R6.Pin_0
  N20: LED1.anode, R1.Pin_1

notes:
  8-LED module
  Allan M Schwartz, 2017
  pin1 Vcc
  pin2 GND
  pin3 D8 CS-595 -> 13 OE brown
  pin4 D10 Latch -> 12 STCP orange
  pin5 D11 MOSI -> 14 DS yellow
  pin6 D13 SCLK -> 11 SHCP blue

// code stored in the sketch: 8_led_74595, c.ino
/**
 * \file _8_LEDs_74hc595
 *
 *      test program for 8 LEDs connected to a 74HC595
 *
 * \author Allan M Schwartz, CodeValue
 *      allans@codevalue.net
 *      April 2017
 *
 * \note
 *      References
 *          74HC595 datasheet
 *
 * ASSEMBLY 
 *      connections 
 *      
 *      Arduino Uno 74hc595
 *      ----------  ----------
 * 
 *      D8  select  13 OE
 *      D9  select  n/c
 *      D10 latch   12 ST_CP
 *      D11 MOSI    14 DS
 *      D12 MISO    n/c
 *      R13 SCLK    11 SH_CP
 *                           9  Q7S can float
 *                           10 MR -> Vcc
 */

// D8 Pin connected to enable pin (OE) of 74HC595
const int enablePin = 8;
// D10 Pin connected to latch pin (ST_CP) of 74HC595
const int latchPin = 10;
// D11 Pin connected to DataIn (DS) of 74HC595
const int dataPin = 11;
// D13 Pin connected to clock pin (SH_CP) of 74HC595
const int clockPin = 13;


void setup()
{
    //set pins to output because they are addressed in the main loop
    pinMode(latchPin, OUTPUT);
    pinMode(dataPin, OUTPUT);
    pinMode(clockPin, OUTPUT);
    pinMode(enablePin, OUTPUT);
    Serial.begin(115200);
    Serial.println("reset");
}

void loop()
{
    Serial.println("loop");
    for (byte k = 0; k < 256; k++) {
        write_shift_regs(k);
        Serial.print("\r\nPin States:");
        Serial.print("0x");
        Serial.print(k, 16);
        Serial.print(", or 0b");
        Serial.print(k, 2);
        delay(500);
    }
}

// This method sends bits to the shift register:

void write_shift_regs(byte ledsState)
{
    digitalWrite(clockPin, LOW);
    digitalWrite(enablePin, HIGH);
    digitalWrite(latchPin, LOW);

    // shift the bits out:
    shiftOut(dataPin, clockPin, MSBFIRST, ledsState);
    delay(20);

    // latch and turn on the output so the LEDs can light up:
    digitalWrite(latchPin, HIGH);
    digitalWrite(enablePin, LOW);
}
