# Fritzing sketch 8_led_8_buttons_repaired (saved by Fritzing 0.9.3b)
circuit board: 6.88566cm x 5.36311cm
breadboards: 4

parts:
  S7 = Pushbutton [package="[THT]"]
  S6 = Pushbutton [package="[THT]"]
  S5 = Pushbutton [package="[THT]"]
  S4 = Pushbutton [package="[THT]"]
  S3 = Pushbutton [package="[THT]"]
  S2 = Pushbutton [package="[THT]"]
  S1 = Pushbutton [package="[THT]"]
  S0 = Pushbutton [package="[THT]"]
  LED0 = LED - 5mm [color="Red (633nm)" package="5 mm [THT]"]
  LED2 = LED - 5mm [color="Red (633nm)" package="5 mm [THT]"]
  LED3 = LED - 5mm [color="Red (633nm)" package="5 mm [THT]"]
  LED5 = LED - 5mm [color="Red (633nm)" package="5 mm [THT]"]
  LED6 = LED - 5mm [color="Red (633nm)" package="5 mm [THT]"]
  LED7 = LED - 5mm [color="Red (633nm)" package="5 mm [THT]"]
  U1 = 74HC595 [part_number=74HC595 package="DIP16 [THT]"]
  R0 = Resistor [tolerance=±5% resistance=330 package=THT]
  R1 = Resistor [tolerance=±5% resistance=330 package=THT]
  LED1 = LED - 5mm [color="Red (633nm)" package="5 mm [THT]"]
  LED4 = LED - 5mm [color="Red (633nm)" package="5 mm [THT]"]
  UNO = Arduino Uno (Rev3)
  5V = male pin header, 1 pin [form="♂ (male)"]
  GND = male pin header, 1 pin [form="♂ (male)"]
  R8_10K = RPACK* [package=rpack-sip-pth-5]
  R9_10K = RPACK* [package=rpack-sip-pth-5]
  R2 = Resistor [tolerance=±5% resistance=330 package=THT]
  R3 = Resistor [tolerance=±5% resistance=330 package=THT]
  R4 = Resistor [tolerance=±5% resistance=330 package=THT]
  R5 = Resistor [tolerance=±5% resistance=330 package=THT]
  R6 = Resistor [tolerance=±5% resistance=330 package=THT]
  R7 = Resistor [tolerance=±5% resistance=330 package=THT]
  U2 = IC, DIP package, 16 pins [chip_label=74165 part_number=74HC165]

nets:
  N1: S7.Pin_1, S7.Pin_2, R9_10K.5, U2.pin6
  GND: S7.Pin_3, S7.Pin_4, S6.Pin_3, S6.Pin_4, S5.Pin_3, S5.Pin_4, S4.Pin_3, S4.Pin_4, S3.Pin_3, S3.Pin_4, S2.Pin_3, S2.Pin_4, S1.Pin_3, S1.Pin_4, S0.Pin_3, S0.Pin_4, LED0.cathode, LED2.cathode, LED3.cathode, LED5.cathode, LED6.cathode, LED7.cathode, U1.GND, U1.OE, LED1.cathode, LED4.cathode, UNO.GND, GND.pin1, U2.pin8
  N2: S6.Pin_1, S6.Pin_2, R9_10K.4, U2.pin5
  N3: S5.Pin_1, S5.Pin_2, R9_10K.3, U2.pin4
  N4: S4.Pin_1, S4.Pin_2, R9_10K.2, U2.pin3
  N5: S3.Pin_1, S3.Pin_2, R8_10K.5, U2.pin14
  N6: S2.Pin_1, S2.Pin_2, R8_10K.4, U2.pin13
  N7: S1.Pin_1, S1.Pin_2, R8_10K.3, U2.pin12
  N8: S0.Pin_1, S0.Pin_2, R8_10K.2, U2.pin11
  N9: LED0.anode, R0.Pin_0
  N10: LED2.anode, R2.Pin_0
  N11: LED3.anode, R3.Pin_0
  N12: LED5.anode, R5.Pin_0
  N13: LED6.anode, R6.Pin_0
  N14: LED7.anode, R7.Pin_0
  N15: U1.Q1, R1.Pin_1
  N16: U1.Q2, R2.Pin_1
  N17: U1.Q3, R3.Pin_1
  N18: U1.Q4, R4.Pin_1
  N19: U1.Q5, R5.Pin_1
  N20: U1.Q6, R6.Pin_1
  N21: U1.Q7, R7.Pin_1
  5V: U1.MR, U1.VCC, UNO.5V, 5V.pin1, R8_10K.1, R9_10K.1, U2.pin16
  SCLK: U1.SH_CP, UNO.D13/SCK, U2.pin2
  STORE: U1.ST_CP, UNO.D10_PWM/SS
  MOSI: U1.DS, UNO.D11_PWM/MOSI
  N22: U1.Q0, R0.Pin_1
  N23: R1.Pin_0, LED1.anode
  N24: LED4.anode, R4.Pin_0
  LOAD: UNO.D9_PWM, U2.pin1
  MISO: UNO.D12/MISO, U2.pin9

notes:
  74165
  pin 1 _PL -> D9 (LOAD)
  pin 2 CP -> D13 (SCLK)
  pin 3,4,5,6 Buttons
  pin 7 _Q7 -> n/c
  pin 8 GND
  pin 9 Q7 -> D12 (MISO)
  pin 10 DS -> GND
  pin 11,12,13,14 Buttons
  pin 15 _CE -> GND
  pin 16 VCC
  8 LEDs 8 Buttons
  v1.1 © A.M. Schwartz, 2017
  SCLK
  MISO
  MOSI
  STORE
  LOAD
  VCC
  GND
  74595
  pin 1-7 -> LED1-7
  pin 8 GND
  pin 9 Q7S -> n/c
  pin 10 _MR _> VCC
  pin 11 SHCP -> D13 (SCLK)
  pin 12 STCP -> D10 (STORE)
  pin 13 _OE -> GND
  pin 14 DS -> D11 (MOSI)
  pin 15 Q0 -> LED0
