# Fritzing sketch neopixel_clock_WeMos, v1.1 (saved by Fritzing 0.9.3b)
circuit board: 9.00001cm x 9.00001cm

parts:
  WeMos_D1_Mini = WeMos D1 Mini
  NeoPixel24 = 24 NeoPixel Ring [part_number=1586]
  NeoPixel12 = 12 NeoPixel Ring [part_number=1643]
  C1 = Electrolytic Capacitor [capacitance=0.47mF package="100 mil [THT, electrolytic]"]
  R1 = Resistor [tolerance=±5% resistance=470 package="1206 [SMD]"]

nets:
  5V: WeMos_D1_Mini.5V, NeoPixel24.VDD, NeoPixel12.VDD, C1.+
  pixel data: WeMos_D1_Mini.D6, R1.Pin_1
  GND: WeMos_D1_Mini.G, NeoPixel24.GND, NeoPixel12.GND, C1.-
  N1: NeoPixel24.IN, NeoPixel12.OUT
  N2: NeoPixel12.IN, R1.Pin_0

notes:
  Allan's NeoPixel Clock
  © 2017 AMSchwartz; v1.1 2017-09-28
  Allan's NeoPixel Clock, 1.1

custom parts:
  24 NeoPixel Ring: 24 ultra bright smart LED NeoPixels are arranged in a circle with 2.6" (66mm) outer diameter. The rings are 'chainable' - connect the output pin of one to the input pin of another. Use only one microcontroller pin to control as many as you can chain together! Each LED is addressable as the driver chip is inside the LED. Each one has ~18mA constant current drive so the color will be very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
  12 NeoPixel Ring: 12 ultra bright smart LED NeoPixels are arranged in a circle with 1.5" (37mm) outer diameter. The rings are 'chainable' - connect the output pin of one to the input pin of another. Use only one microcontroller pin to control as many as you can chain together! Each LED is addressable as the driver chip is inside the LED. Each one has ~18mA constant current drive so the color will be very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
