# Fritzing sketch dip switch, resistor network (saved by Fritzing 0.9.3b)
breadboards: 1

parts:
  Part1 = Arduino Nano (Rev3.0) (ICSP)
  DIP_SWITCH = DIP Switch 4 Position [package=dipswitch-04]
  R1 = Resistor [tolerance=±5% resistance=10k package=THT]
  R2 = Resistor [tolerance=±5% resistance=20k package=THT]
  R3 = Resistor [tolerance=±5% resistance=40k package=THT]
  R4 = Resistor [tolerance=±5% resistance=80k package=THT]
  R5 = Resistor [tolerance=±5% resistance=10k package=THT]

nets:
  GND: Part1.GND, R5.Pin_0
  5V: Part1.5V, DIP_SWITCH.1, DIP_SWITCH.2, DIP_SWITCH.3, DIP_SWITCH.4
  buttons: Part1.A0, R1.Pin_1, R2.Pin_1, R3.Pin_1, R4.Pin_1, R5.Pin_1
  N1: DIP_SWITCH.5, R4.Pin_0
  N2: DIP_SWITCH.6, R3.Pin_0
  N3: DIP_SWITCH.7, R2.Pin_0
  N4: DIP_SWITCH.8, R1.Pin_0
