# Fritzing sketch dip switch, simpliest hookup (saved by Fritzing 0.9.3b)
breadboards: 1

parts:
  Part1 = Arduino Nano (Rev3.0) (ICSP)
  SW1 = DIP Switch 4 Position [package=dipswitch-04]

nets:
  N1: Part1.GND, SW1.1, SW1.2, SW1.3, SW1.4
  N2: Part1.D2, SW1.8
  N3: Part1.D3, SW1.7
  N4: Part1.D4, SW1.6
  N5: Part1.D5, SW1.5
